# Fritzing sketch 8d5a105f-6e61-46d1-a160-2962547bdaee (saved by Fritzing 0.9.3b)
breadboards: 1

parts:
  S1 = Pushbutton [package="[THT]"]
  S2 = Pushbutton [package="[THT]"]
  U1 = SWITCH-SPST-2 [package=switch-spst-vertical]
  SPKR1 = Loudspeaker
  MIC1 = Microphone
  U2 = LIPO-1000mAh [package=lipo-1000]
  R2 = Resistor [tolerance=±5% resistance=220 package="0402 [SMD]"]
  R1 = Resistor [tolerance=±5% resistance=220 package="0402 [SMD]"]
  ESP-12F1 = ESP-12F

nets:
  N1: S1.Pin_1, S1.Pin_2, S2.Pin_1, S2.Pin_2, U1.O, SPKR1.pin1, U2.+
  N2: S1.Pin_3, S1.Pin_4, S2.Pin_3, S2.Pin_4, U2.-, R2.Pin_1, R1.Pin_1
  N3: U1.P, ESP-12F1.GPIO14, ESP-12F1.GPIO12, ESP-12F1.GPIO13, ESP-12F1.VCC
  N4: SPKR1.pin2, MIC1.pin2, ESP-12F1.REST, ESP-12F1.ADC
  N5: R2.Pin_0, ESP-12F1.GPIO4
  N6: R1.Pin_0, ESP-12F1.RXD, ESP-12F1.TXD
  N7: ESP-12F1.GND, ESP-12F1.GPIO15, ESP-12F1.GPIO2, ESP-12F1.GPIO0

custom parts:
  ESP-12F: ESP-12F WiFi module is developed by Ai-thinker Team. core processor ESP8266 in smaller sizes of the module encapsulates Tensilica L106 integrates industry-leading ultra low power 32-bit MCU micro, with the 16-bit short mode, Clock speed support 80 MHz, 160 MHz, supports the RTOS, integrated Wi-Fi MAC/BB/RF/PA/LNA, on-board antenna. The module supports standard IEEE802.11 b/g/n agreement,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
